// Logisim project FaCircuit.circ as structural Verilog: 9 circuits, main circuit MainCircuit
module Fa (
  input  w,
  input  x,
  input  y,
  input  z,
  output out_5
);

  wire and_1_out, and_2_out, and_3_out, not_1_out, not_2_out, not_3_out, xnor_1_out;

  not not_1 (not_1_out, w);
  not not_2 (not_2_out, x);
  not not_3 (not_3_out, y);
  and and_1 (and_1_out, not_1_out, xnor_1_out);
  xnor xnor_1 (xnor_1_out, x, z);
  and and_2 (and_2_out, not_1_out, y);
  and and_3 (and_3_out, w, not_2_out, not_3_out);
  or or_1 (out_5, and_1_out, and_2_out, and_3_out);
endmodule

module BCD_to_7_segment (
  input  w,
  input  x,
  input  y,
  input  z,
  output out_5,
  output out_6,
  output out_7,
  output out_8,
  output out_9,
  output out_10,
  output out_11
);

  Fa Fa (.w(w), .x(x), .y(y), .z(z), .out_5(out_5));
  Fb Fb (.w(w), .x(x), .y(y), .z(z), .out_5(out_6));
  Fc Fc (.w(w), .out_5(out_7), .x(x), .y(y), .z(z));
  Fd Fd (.w(w), .x(x), .out_5(out_8), .y(y), .z(z));
  Fe Fe (.w(w), .x(x), .out_5(out_9), .y(y), .z(z));
  Ff Ff (.w(w), .x(x), .out_5(out_10), .y(y), .z(z));
  Fg Fg (.w(w), .x(x), .out_5(out_11), .y(y), .z(z));
  _7_Segment_Display u_7_segment_display_1 (.g(out_11), .a(out_5), .b(out_6));  // open: f, e, d, c, dp
endmodule

module Fb (
  input  w,
  input  x,
  input  y,
  input  z,
  output out_5
);

  wire and_1_out, and_2_out, not_1_out, not_2_out, not_3_out, or_1_out, xnor_1_out;

  not not_1 (not_1_out, w);
  not not_2 (not_2_out, x);
  not not_3 (not_3_out, y);
  or or_1 (or_1_out, not_1_out, not_3_out);
  xnor xnor_1 (xnor_1_out, y, z);
  and and_1 (and_1_out, or_1_out, not_2_out);
  and and_2 (and_2_out, not_1_out, xnor_1_out);
  or or_2 (out_5, and_1_out, and_2_out);
endmodule

module Fc (
  input  w,
  input  x,
  input  y,
  input  z,
  output out_5
);

  wire and_1_out, and_2_out, not_1_out, not_2_out, not_3_out, or_1_out;

  not not_1 (not_1_out, w);
  not not_2 (not_2_out, x);
  not not_3 (not_3_out, y);
  or or_1 (or_1_out, x, z);
  and and_1 (and_1_out, not_2_out, not_3_out);
  and and_2 (and_2_out, not_1_out, or_1_out);
  or or_2 (out_5, and_1_out, and_2_out);
endmodule

module Fd (
  input  w,
  input  x,
  input  y,
  input  z,
  output out_5
);

  wire and_1_out, and_2_out, and_3_out, and_4_out, and_5_out, not_1_out, not_2_out, not_3_out, not_4_out,
       or_1_out, or_2_out;

  not not_1 (not_1_out, w);
  not not_2 (not_2_out, x);
  not not_3 (not_3_out, y);
  not not_4 (not_4_out, z);
  or or_1 (or_1_out, y, not_4_out);
  and and_1 (and_1_out, not_2_out, or_1_out);
  and and_2 (and_2_out, y, not_4_out);
  and and_3 (and_3_out, x, not_3_out, z);
  and and_4 (and_4_out, not_2_out, w, not_3_out);
  or or_2 (or_2_out, and_1_out, and_2_out, and_3_out);
  and and_5 (and_5_out, not_1_out, or_2_out);
  or or_3 (out_5, and_4_out, and_5_out);
endmodule

module Fe (
  input  w,
  input  x,
  input  y,
  input  z,
  output out_5
);

  wire and_1_out, and_2_out, not_1_out, not_2_out, not_3_out, not_4_out, or_1_out;

  not not_1 (not_1_out, w);
  not not_2 (not_2_out, x);
  not not_3 (not_3_out, y);
  not not_4 (not_4_out, z);
  and and_1 (and_1_out, not_1_out, y);
  and and_2 (and_2_out, not_2_out, not_3_out);
  or or_1 (or_1_out, and_1_out, and_2_out);
  and and_3 (out_5, or_1_out, not_4_out);
endmodule

module Ff (
  input  w,
  input  x,
  input  y,
  input  z,
  output out_5
);

  wire and_1_out, and_2_out, and_3_out, and_4_out, not_1_out, not_2_out, not_3_out, not_4_out, or_1_out,
       or_2_out;

  not not_1 (not_1_out, y);
  not not_2 (not_2_out, z);
  not not_3 (not_3_out, w);
  not not_4 (not_4_out, x);
  or or_1 (or_1_out, x, not_2_out);
  and and_1 (and_1_out, or_1_out, not_1_out);
  and and_2 (and_2_out, not_2_out, x);
  or or_2 (or_2_out, and_1_out, and_2_out);
  and and_3 (and_3_out, w, not_4_out, not_1_out);
  and and_4 (and_4_out, not_3_out, or_2_out);
  or or_3 (out_5, and_3_out, and_4_out);
endmodule

module Fg (
  input  w,
  input  x,
  input  y,
  input  z,
  output out_5
);

  wire and_1_out, and_2_out, and_3_out, and_4_out, not_1_out, not_2_out, not_3_out, not_4_out, or_1_out,
       xor_1_out;

  not not_1 (not_1_out, w);
  not not_2 (not_2_out, y);
  not not_3 (not_3_out, z);
  not not_4 (not_4_out, x);
  and and_1 (and_1_out, y, not_3_out);
  and and_2 (and_2_out, x, not_2_out);
  xor xor_1 (xor_1_out, w, y);
  or or_1 (or_1_out, and_1_out, and_2_out);
  and and_3 (and_3_out, not_4_out, xor_1_out);
  and and_4 (and_4_out, not_1_out, or_1_out);
  or or_2 (out_5, and_3_out, and_4_out);
endmodule

module MainCircuit (
  input  w,
  input  x,
  input  y,
  input  z
);

  wire BCD_to_7_segment_out_5, BCD_to_7_segment_out_6, BCD_to_7_segment_out_7, BCD_to_7_segment_out_8,
       BCD_to_7_segment_out_9, BCD_to_7_segment_out_10, BCD_to_7_segment_out_11;

  BCD_to_7_segment BCD_to_7_segment (
    .w(w), .x(x), .y(y), .z(z), .out_5(BCD_to_7_segment_out_5), .out_6(BCD_to_7_segment_out_6),
    .out_7(BCD_to_7_segment_out_7), .out_8(BCD_to_7_segment_out_8), .out_9(BCD_to_7_segment_out_9),
    .out_10(BCD_to_7_segment_out_10), .out_11(BCD_to_7_segment_out_11));
  _7_Segment_Display u_7_segment_display_1 (
    .g(BCD_to_7_segment_out_11), .f(BCD_to_7_segment_out_10), .a(BCD_to_7_segment_out_5),
    .b(BCD_to_7_segment_out_6), .e(BCD_to_7_segment_out_9), .d(BCD_to_7_segment_out_8),
    .c(BCD_to_7_segment_out_7));  // open: dp
endmodule
